# Fritzing sketch RGB led strip driver2 (saved by Fritzing 0.9.6b)
circuit board: 5.88891cm x 4.14558cm
breadboards: 1
perfboards: 1

parts:
  WeMos_D1_Mini1 = WeMos D1 Mini
  ULN2003A = ULN2003A [package="DIP16 [THT]"]
  Power_plug1 = Power plug
  Mini-360_DC-DC_Buck_converter = Mini-360 DC-DC Buck converter [package=THT]
  JP3 = Header 4 [package=screwterminal-3.5mm-4_lock]
  JP4 = Header 4 [package=screwterminal-3.5mm-4_lock]
  J1 = Camdenboss CTB0158-2 [part_number=CTB0158-2 package=THT]
  S2 = SPST Switch [package=switch-spdt-smd]
  S1 = SPST Switch [package=switch-spdt]  # not connected

nets:
  N1: WeMos_D1_Mini1.5V, Mini-360_DC-DC_Buck_converter.OUT+
  N2: WeMos_D1_Mini1.D5, ULN2003A.In_1
  N3: WeMos_D1_Mini1.D6, ULN2003A.In_3
  N4: WeMos_D1_Mini1.D7, ULN2003A.In_2
  N5: WeMos_D1_Mini1.G, ULN2003A.0V, Mini-360_DC-DC_Buck_converter.OUT-
  N6: ULN2003A.COM_-_Common, Mini-360_DC-DC_Buck_converter.IN+, JP3.1, JP4.1, S2.S
  N7: ULN2003A.Out_3, JP3.2, JP4.2
  N8: ULN2003A.Out_2, JP3.3, JP4.3
  N9: ULN2003A.Out_1, JP3.4, JP4.4
  N10: Power_plug1.GND, Mini-360_DC-DC_Buck_converter.IN-, J1.pin2
  N11: Power_plug1.VCC, S2.P
  N12: J1.pin1, S2.O

notes:
  12V 5A DC Input
  Simple 5050 RGB led strip
  2 Connectors for both sides of the PCB
  12V to 5V DC Buck converter

custom parts:
  Mini-360 DC-DC Buck converter: Mini-360 DC-DC Buck converter. Tiny buck step down voltage converter, input voltage 4.75 to 23V output 1 to 17V adjustable. Available from ebay and the like.
